# Fritzing sketch Final Fritz Sketch (saved by Fritzing 0.9.3b)
breadboards: 1

parts:
  Part1 = Photon
  Part5 = Arduino Motor Shield
  Adafruit_Atmega32u1 = Adafruit Atmega32u4 Breakout Board [part_number="Atmega 32u4"]

nets:
  N1: Part1.RX, Part5.RX, Adafruit_Atmega32u1.D0
  N2: Part1.TX, Part5.TX, Adafruit_Atmega32u1.D1
  GND: Part1.GND, Adafruit_Atmega32u1.GND
